# Fritzing sketch Stepper_ultra_keypad (saved by Fritzing 0.9.3b)
breadboards: 1

parts:
  Part1 = Arduino Uno (Rev3)
  IC1 = H-Bridge [package=THT]
  M1 = Stepper Motor - Bipolar
  hc-sr1 = hc-sr04
  Matrix_keypad1 = KEYPAD 4x4

nets:
  N1: Part1.D8, Matrix_keypad1.row2
  N2: Part1.D9_PWM, Matrix_keypad1.row1
  N3: Part1.D10_PWM/SS, Matrix_keypad1.col4
  N4: Part1.D11_PWM/MOSI, Matrix_keypad1.col3
  N5: Part1.D12/MISO, Matrix_keypad1.col2
  N6: Part1.D13/SCK, Matrix_keypad1.col1
  N7: Part1.D0/RX, IC1.1A, M1.A
  N8: Part1.D1/TX, Matrix_keypad1.row4
  N9: Part1.D2, hc-sr1.Trig
  N10: Part1.D3_PWM, hc-sr1.Echo
  N11: Part1.D4, IC1.3A
  N12: Part1.D5_PWM, IC1.4A
  N13: Part1.D6_PWM, IC1.2A
  N14: Part1.D7, Matrix_keypad1.row3
  N15: Part1.3V3, IC1.VCC2
  5V: Part1.5V, hc-sr1.VCC
  GND: Part1.GND, IC1.GND3, hc-sr1.GND
  N16: IC1.2Y, M1.C
  N17: IC1.3Y, M1.B
  N18: IC1.4Y, M1.D

custom parts:
  KEYPAD 4x4: Matrix keypad 16 buttons, 4 rows x 4 columns

// code stored in the sketch: rep_stepper_ultra_keypad.ino
Stepper myStepper(stepsPerRevolution, 8, 9, 10, 11);

void setup() {
  myStepper.setSpeed(100);
  Serial.begin(9600);
}

void loop() {
  // 1 rotation clockwise: 
  Serial.println("clockwise");
  myStepper.step(stepsPerRevolution);
  delay(2000);

  // 1 rotation counterclockwise:
  Serial.println("counterclockwise");
  myStepper.step(-stepsPerRevolution);
  delay(2000);
}
